# Fritzing sketch 007 (saved by Fritzing 0.9.9b)
breadboards: 1

parts:
  R14 = Resistor [tolerance=±5% power=0.25 resistance=180 package=THT]
  LED5 = LED - 3mm [color="Green (555nm)" current=0.030 package="3 mm [THT]"]
  1x_WeMos_D1_Mini1 = WeMos D1 Mini  # not connected
  LED6 = LED - 3mm [color="Green (555nm)" current=0.030 package="3 mm [THT]"]
  LED7 = LED - 3mm [color="Green (555nm)" current=0.030 package="3 mm [THT]"]
  LED8 = LED - 3mm [color="Green (555nm)" current=0.030 package="3 mm [THT]"]
  LED9 = LED - 3mm [color="Green (555nm)" current=0.030 package="3 mm [THT]"]
  R15 = Resistor [tolerance=±5% power=0.25 resistance=180 package=THT]
  R16 = Resistor [tolerance=±5% power=0.25 resistance=180 package=THT]
  R17 = Resistor [tolerance=±5% power=0.25 resistance=180 package=THT]
  R18 = Resistor [tolerance=±5% power=0.25 resistance=180 package=THT]

nets:
  N1: R14.Pin_0, LED5.anode
  N2: LED5.cathode, LED6.cathode, LED7.cathode, LED8.cathode, LED9.cathode
  N3: LED6.anode, R15.Pin_0
  N4: LED7.anode, R16.Pin_0
  N5: LED8.anode, R17.Pin_0
  N6: LED9.anode, R18.Pin_0
