# Fritzing sketch 008 (saved by Fritzing 0.9.9b)
breadboards: 1

parts:
  R14 = Resistor [tolerance=±5% power=0.25 resistance=180 package=THT]
  LED5 = LED - 3mm [color="Green (555nm)" current=0.030 package="3 mm [THT]"]
  1x_WeMos_D1_Mini1 = WeMos D1 Mini  # not connected

nets:
  N1: R14.Pin_0, LED5.anode
