# Fritzing sketch 010 (saved by Fritzing 0.9.9b)
breadboards: 1

parts:
  5x_Widerstand = Resistor [tolerance=±5% power=0.25 resistance=180 package=THT]
  1x_LED_weiß = LED - 5mm [color="White (6500K)" current=0.030 package="5 mm [THT]"]
  3x_NPN_Transistor = NPN-Transistor [package="TO92 [THT]"]
  1x_WeMos_D1_Mini1 = WeMos D1 Mini  # not connected

nets:
  N1: 5x_Widerstand.Pin_0, 1x_LED_weiß.anode
  N2: 1x_LED_weiß.cathode, 3x_NPN_Transistor.C
