# Fritzing sketch 011 (saved by Fritzing 0.9.4)
breadboards: 1

parts:
  5x_Widerstand = Resistor [tolerance=±5% power=0.25 resistance=180 package=THT]
  R11 = Resistor [tolerance=±5% power=0.25 resistance=180 package=THT]
  R12 = Resistor [tolerance=±5% power=0.25 resistance=180 package=THT]
  R13 = Resistor [tolerance=±5% power=0.25 resistance=180 package=THT]
  R14 = Resistor [tolerance=±5% power=0.25 resistance=180 package=THT]
  5x_LED_grün = LED - 3mm [color="Green (555nm)" current=0.030 package="3 mm [THT]"]
  LED2 = LED - 3mm [color="Green (555nm)" current=0.030 package="3 mm [THT]"]
  LED3 = LED - 3mm [color="Green (555nm)" current=0.030 package="3 mm [THT]"]
  LED4 = LED - 3mm [color="Green (555nm)" current=0.030 package="3 mm [THT]"]
  LED5 = LED - 3mm [color="Green (555nm)" current=0.030 package="3 mm [THT]"]
  1x_8bit_Schieberegister = 74HC595 [package="DIP16 [THT]"]
  1x_WeMos_D1_Mini1 = WeMos D1 Mini  # not connected

nets:
  N1: 5x_Widerstand.Pin_0, 5x_LED_grün.anode
  N2: 5x_Widerstand.Pin_1, 1x_8bit_Schieberegister.Q0
  N3: R11.Pin_0, LED3.anode
  N4: R11.Pin_1, 1x_8bit_Schieberegister.Q1
  N5: R12.Pin_0, LED4.anode
  N6: R12.Pin_1, 1x_8bit_Schieberegister.Q2
  N7: R13.Pin_0, LED5.anode
  N8: R13.Pin_1, 1x_8bit_Schieberegister.Q3
  N9: R14.Pin_0, LED2.anode
  N10: R14.Pin_1, 1x_8bit_Schieberegister.Q4
  N11: 5x_LED_grün.cathode, LED2.cathode, LED3.cathode, LED4.cathode, LED5.cathode, 1x_8bit_Schieberegister.GND, 1x_8bit_Schieberegister.OE
  N12: 1x_8bit_Schieberegister.MR, 1x_8bit_Schieberegister.VCC
