# Fritzing sketch 020 (saved by Fritzing 0.9.9b)
breadboards: 1

parts:
  max_3_3V = WeMos D1 Mini  # not connected
  R1 = Resistor [tolerance=±5% power=0.25 resistance=10k package=THT]
  R2 = Resistor [tolerance=±5% power=0.25 resistance=22k package=THT]
  VCC1 = Battery block 9V
  D1 = Rectifier Diode [part_number=1N4001 package="300 mil [THT]"]

nets:
  N1: R1.Pin_0, VCC1.-
  N2: R1.Pin_1, R2.Pin_0
  N3: R2.Pin_1, D1.cathode
  N4: VCC1.+, D1.anode
