# Fritzing sketch 022 (saved by Fritzing 0.9.4)
breadboards: 1

parts:
  R3 = Resistor [tolerance=±5% power=0.25 resistance=10k package=THT]
  S3 = Pushbutton [package="[THT]"]
  1x_WeMos_D1_Mini1 = WeMos D1 Mini  # not connected

nets:
  N1: R3.Pin_0, S3.Pin_3, S3.Pin_4
  N2: S3.Pin_1, S3.Pin_2
