# Fritzing sketch 123 (saved by Fritzing 0.9.4)
breadboards: 1

parts:
  R6 = Resistor [tolerance=±5% power=0.25 resistance=120 package=THT]
  R8 = Resistor [tolerance=±5% power=0.25 resistance=120 package=THT]
  R9 = Resistor [tolerance=±5% power=0.25 resistance=120 package=THT]
  1x_LED_RGB = RGB LED (com. cathode, rgb) [package="5 mm [THT]"]
  1x_WeMos_D1_Mini1 = WeMos D1 Mini  # not connected

nets:
  N1: R6.Pin_0, 1x_LED_RGB.red_anode
  N2: R8.Pin_0, 1x_LED_RGB.green_anode
  N3: R9.Pin_0, 1x_LED_RGB.blue_anode
