# Fritzing sketch 007 (saved by Fritzing 0.9.9b)
breadboards: 1

parts:
  Q1 = NPN-Transistor [package="TO92 [THT]"]
  1x_WeMos_D1_Mini1 = WeMos D1 Mini  # not connected
  1x_NeoPixel_Jewel = NeoPixel Jewel [part_number=2226]
  J1 = male pin header, 3 pins [form="♂ (male)"]

nets:
  N1: Q1.E, 1x_NeoPixel_Jewel.VDD, J1.pin2
  N2: Q1.C, 1x_NeoPixel_Jewel.IN, J1.pin1
  N3: 1x_NeoPixel_Jewel.GND, J1.pin3

custom parts:
  NeoPixel Jewel: We fit seven of our tiny 5050 (5mm x 5mm) smart RGB LEDs onto a beautiful, round PCB with mounting holes and a chainable design to create what we think is our most elegant (and evening-wear appropriate) NeoPixel board yet. Use only one microcontroller pin to control as many as you can chain together! Each LED is addressable as the driver chip is inside the LED. Each one has ~18mA constant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
