# Fritzing sketch 011 (saved by Fritzing 1.0.1rc)
breadboards: 1

parts:
  R14 = Resistor [tolerance=±5% power=0.25 resistance=180 package=THT]
  LED5 = LED - 3mm [color="Green (555nm)" current=0.030 package="3 mm [THT]"]
  1x_WeMos_D1_Mini1 = WeMos D1 Mini  # not connected
  S1 = Pushbutton [package="[THT]"]
  R15 = Resistor [tolerance=±5% power=0.25 resistance=10k package=THT]

nets:
  N1: R14.Pin_0, LED5.anode
  N2: LED5.cathode, R15.Pin_1
  N3: S1.Pin_1, S1.Pin_2, R15.Pin_0
  N4: S1.Pin_3, S1.Pin_4
