# Fritzing sketch 013 (saved by Fritzing 1.0.1rc)
breadboards: 1

parts:
  1x_WeMos_D1_Mini1 = WeMos D1 Mini  # not connected
  R1 = Resistor [tolerance=±5% power=0.25 resistance=10k package=THT]
  R2 = Resistor [tolerance=±5% power=0.25 resistance=10k package=THT]

nets:
  N1: R1.Pin_0, R2.Pin_1
