# Fritzing sketch Wetterstation (saved by Fritzing 1.0.1rc)
breadboards: 1

parts:
  Mod1 = Amica NodeMCU DEVKIT 1.0
  DHT1 = DHT22 Humidity and Temperature Sensor
  Bauteil1 = VEML6070 [part_number=VEML6070]
  Bauteil2 = Adafruit TSL2561 [part_number="Adafruit #439"]
  Bauteil3 = Adafruit ADS1115 16Bit I2C ADC [part_number="Adafruit #1085"]
  Bauteil4 = Soil Moisture Sensor
  R1 = Temperature Sensor (Thermistor) [thermistor_type=NTC package=THT]
  BMP280_Breakout1 = BMP280 Breakout Board [part_number=BMP280]
  Bauteil5 = AS3935 lightning sensor breakout
  U1 = MLX90614 [package=to-39]
  Bauteil6 = Triple Axis Magnetometer - HMC5883 Breakout

nets:
  VDD: Mod1.pin1, Mod1.pin_10, Mod1.pin_26, DHT1.VDD, Bauteil1.VDD, Bauteil1.ACK, Bauteil2.VIN, Bauteil3.AIN0, Bauteil3.VDD, Bauteil4.VCC, R1.pin_1, BMP280_Breakout1.VCC, Bauteil5.VCC, U1.VDD, Bauteil6.VCC
  GND: Mod1.pin2, Mod1.pin_9, Mod1.pin_25, Mod1.pin_29, DHT1.GND, Bauteil1.GND, Bauteil2.GND, Bauteil3.GND, Bauteil4.GND, BMP280_Breakout1.GND, Bauteil5.gnd, U1.VSS, Bauteil6.GND
  N1: Mod1.pin_12, DHT1.DATA
  N2: Mod1.pin_13, Bauteil1.SDA, Bauteil2.SDA, Bauteil3.SDA, BMP280_Breakout1.SDA, Bauteil5.SDA, U1.PWM_SDA, Bauteil6.SDA
  N3: Mod1.pin_14, Bauteil1.SCL, Bauteil2.SCL, Bauteil3.SCL, BMP280_Breakout1.SCL, Bauteil5.SCL, U1.SCL_VZ, Bauteil6.SCL
  N4: Bauteil3.AIN2, R1.pin_0
  N5: Bauteil3.AIN1, Bauteil4.SIG

custom parts:
  VEML6070: This little sensor is a great way to add UV light sensing to any microcontroller project. The VEML6070 from Vishay has a true UV A light sensor and an I2C-controlled ADC that will take readings and integrate them for you over ~60ms to 500ms.
  Adafruit TSL2561: The TSL2561 luminosity sensor is an advanced digital light sensor, ideal for use in a wide range of light situations. Compared to low cost CdS cells, this sensor is more precise, allowing for exact lux calculations and can be configured for different gain/timing ranges to detect light ranges from up to 0.1 - 40,000+ Lux on the fly. The best part of this sensor is that it contains both infrared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
  Adafruit ADS1115 16Bit I2C ADC: For microcontrollers without an analog-to-digital converter or when you want a higher-precision ADC, the ADS1115 provides 16-bit precision at 860 samples/second over I2C. The chip can be configured as 4 single-ended input channels, or two differential channels. As a nice bonus, it even includes a programmable gain amplifier, up to x16, to help boost up smaller single/differential signals to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
  BMP280 Breakout Board: This is a breakout board for the Bosch Sensortec BMP280, "an absolute barometric pressure sensor especially designed for mobile applications." The operation range is 300 to 1100 hPa. Supply voltage is 1.2 to 3.6V. Operating temperature range is -40 to +85 °C.
  AS3935 lightning sensor breakout: lightning sensor breakout
